// Logisim project p6.circ as structural Verilog: 1 circuit, main circuit main
module main (
  input  A,
  input  B,
  input  D,
  input  C,
  output A_BC_D
);

  wire and_1_out;

  and and_1 (and_1_out, B, C);
  or or_1 (A_BC_D, A, and_1_out, D);

  // Notes on the sheet:
  //   1601CS46
  //   SIDDHARTH THAKUR
  //   OUTPUT
endmodule
